# Fritzing sketch ＵＩ付きユニバーサル基板 (saved by Fritzing 0.9.5d)
circuit board: 6.44649cm x 5.72043cm
breadboards: 1

parts:
  J1 = Raspberry Pi Header 40pin [package=THT]
  SW-1 = Momentary Switch [package=ksa_sealed_tac_switch]
  J2 = Raspberry Pi Header 40pin [package=THT]
  SW-2 = Momentary Switch [package=ksa_sealed_tac_switch]
  LED = Resistor [tolerance=±5% resistance=220 power=0.25 package=THT]
  LED1 = LED - 3mm [color="Red (633nm)" current=0.030 package="3 mm [THT]"]
  LED2 = LED - 3mm [color="Red (633nm)" current=0.030 package="3 mm [THT]"]
  LED_2 = Resistor [tolerance=±5% resistance=220 power=0.25 package=THT]
  R3 = Resistor [tolerance=±5% resistance=220 power=0.25 package=THT]
  R4 = Resistor [tolerance=±5% resistance=220 power=0.25 package=THT]
  R5 = Resistor [tolerance=±5% resistance=220 power=0.25 package=THT]
  R6 = Resistor [tolerance=±5% resistance=220 power=0.25 package=THT]

nets:
  3V3: J1.3V3, SW-1.3, J2.3V3, SW-2.3
  5V: J1.5V, J2.5V
  N1: J1.GPIO2, J2.GPIO2
  N2: J1.IO3, J2.IO3
  GND: J1.GND, J2.GND, LED1.cathode, LED2.cathode, R3.Pin_0, R4.Pin_0
  N3: J1.IO4, J2.IO4
  N4: J1.IO14, J2.IO14
  N5: J1.IO15, J2.IO15
  N6: J1.IO17, J2.IO17, LED_2.Pin_1
  N7: J1.IO18, J2.IO18
  N8: J1.IO27, J2.IO27, LED.Pin_1
  N9: J1.IO22, J2.IO22
  N10: J1.IO23, J2.IO23
  N11: J1.IO24, J2.IO24
  N12: J1.IO10, J2.IO10
  N13: J1.IO9, J2.IO9
  N14: J1.IO25, J2.IO25
  N15: J1.IO11, J2.IO11
  N16: J1.IO8, J2.IO8
  N17: J1.IO7, J2.IO7
  N18: J1.IO0, J2.IO0
  N19: J1.IO1, J2.IO1
  N20: J1.IO5, J2.IO5, R5.Pin_0
  N21: J1.IO6, J2.IO6, R6.Pin_1
  N22: J1.IO12, J2.IO12
  N23: J1.IO13, J2.IO13
  N24: J1.IO19, J2.IO19
  N25: J1.IO16, J2.IO16
  N26: J1.IO26, J2.IO26
  N27: J1.IO20, J2.IO20
  N28: J1.IO21, J2.IO21
  N29: SW-1.1, R4.Pin_1, R5.Pin_1
  N30: SW-2.1, R3.Pin_1, R6.Pin_0
  N31: LED.Pin_0, LED2.anode
  N32: LED1.anode, LED_2.Pin_0

notes:
  TKJ-seisakusho Universal-基板-v02
  NC
  5V
  DC-Jack
  GND
  ●
  3.3V
  TKJ-Works
  https://raspi.thebase.in/
  ＵＩ付きユニバーサル基板
  このデータは自由に使ってください。
  その他拡張基板は
  スイッチサイエンス
  https://www.switch-science.com/
  で「tkj」と検索してもみられます。
  このファィルと同じところに「基板申し込み要領.txt」というのがあります。よろしければ見てください。

custom parts:
  Raspberry Pi Header 40pin: Raspberry Pi 40 pin header - for creating your own shields. (Mar 2020, bb: make breadboard friendly (.4in pin spacing) and add labels. Schematic add labels. PCB make oblong pins to allow routing traces between the pins.)
